# Fritzing sketch FanTach (saved by Fritzing 0.9.4)
perfboards: 1

parts:
  IC1 = IC, DIP package, 14 pins [chip_label=ATTiny24]
  R2 = Resistor [tolerance=±5% resistance=220 package=THT]
  J6 = male pin header, 4 pins [form="♂ (male)"]
  J0 = male pin header, 3 pins [form="♂ (male)"]
  J4 = male pin header, 4 pins [form="♂ (male)"]
  J3 = male pin header, 4 pins [form="♂ (male)"]
  J2 = male pin header, 4 pins [form="♂ (male)"]
  J1 = male pin header, 4 pins [form="♂ (male)"]
  J5 = female pin header, 3 pins [form="♀ (female)"]
  LED2 = LED - 5mm [color="Red (633nm)" package="5 mm [THT]"]
  D1 = Zener Diode [part_number=5V1 breakdown_voltage=5.1V package="300 mil [THT]"]

nets:
  5V: IC1.pin1, R2.Pin_0, J0.pin3
  N1: IC1.pin2, J5.pin2
  N2: IC1.pin3, J5.pin3
  LED: IC1.pin4, LED2.cathode
  PWM_3: IC1.pin5, J4.pin4
  PWM_2: IC1.pin6, J3.pin4
  PWM_1: IC1.pin7, J2.pin4
  PWM_0: IC1.pin8, J1.pin4
  N3: IC1.pin9, J0.pin2, D1.cathode
  TACH_3: IC1.pin10, J4.pin3
  TACH_2: IC1.pin11, J3.pin3
  TACH_1: IC1.pin12, J2.pin3
  TACH_0: IC1.pin13, J1.pin3
  GND: IC1.pin14, J6.pin2, J6.pin3, J0.pin1, J4.pin1, J3.pin1, J2.pin1, J1.pin1, J5.pin1, D1.anode
  N4: R2.Pin_1, LED2.anode
  12V: J6.pin1, J4.pin2, J3.pin2, J2.pin2, J1.pin2

notes:
  Fan Tacho Board, v0.1
